# Fritzing sketch tealight (saved by Fritzing 0.9.3b)
circuit board: 8.46667cm x 5.64444cm
breadboards: 1

parts:
  Part1 = Adafruit Trinket 3V [part_number="Adafruit #1500"]
  R1 = Resistor [tolerance=±5% resistance=220 package="0805 [SMD]"]
  LED1 = LED - 5mm [color="Yellow (592nm)" package="5 mm [THT]"]

nets:
  N1: Part1.GND, LED1.anode
  N2: Part1.#0, R1.Pin_0
  N3: R1.Pin_1, LED1.cathode

custom parts:
  Adafruit Trinket 3V: Trinket may be small, but do not be fooled by its size! It's a tiny microcontroller board, built around the Atmel ATtiny85, a little chip with a lot of power. We wanted to design a microcontroller board that was small enough to fit into any project, and low cost enough to use without hesitation. Perfect for when you don't want to give up your expensive dev-board and you aren't willing to take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

// code stored in the sketch: tealight.ino
#define FLICKER_LED_PIN 0

// the start of the flicker (low)
static int flicker_low_min = 15;
static int flicker_low_max = 175;

// the end value of the flicker (high)
static int flicker_high_min = 180;
static int flicker_high_max = 256;

// delay between each low-high-low cycle
// low->high |flicker_hold| high->low
static int flicker_hold_min = 20; // milliseconds
static int flicker_hold_max = 80; // milliseconds

// delay after each low-high-low cycle
// low->high->low |flicker_pause| low->high...
static int flicker_pause_min = 100; // milliseconds
static int flicker_pause_max = 200;  // milliseconds

// delay low to high and high to low cycle
static int flicker_speed_min = 800; // microseconds
static int flicker_speed_max = 1000; // microseconds

void setup() {
  pinMode(FLICKER_LED_PIN, OUTPUT);
}

int flicker_random_low_start = 0;
int flicker_random_low_end = 0;
int flicker_random_high = 0;
int flicker_random_speed_start = 0;
int flicker_random_speed_end = 0;

void loop() {

  // random time for low
  flicker_random_low_start = random(flicker_low_min, flicker_low_max);
  flicker_random_low_end = random(flicker_low_min, flicker_low_max);

  // random time for high
  flicker_random_high = random(flicker_high_min, flicker_high_max);

  // random time for speed
  flicker_random_speed_start = random(flicker_speed_min, flicker_speed_max);
  flicker_random_speed_end = random(flicker_speed_min, flicker_speed_max);

  // low -> high
  for (int i = flicker_random_low_start; i < flicker_random_high; i++) {
    analogWrite(FLICKER_LED_PIN, i);
    delayMicroseconds(flicker_random_speed_start);
  }

  // hold
  delay(random(flicker_hold_min, flicker_hold_max));

  // high -> low
  for (int i = flicker_random_high; i >= flicker_random_low_end; i--) {
    analogWrite(FLICKER_LED_PIN, i);
    delayMicroseconds(flicker_random_speed_end);
  }

  // pause
  delay(random(flicker_pause_min, flicker_pause_max));
}
